# Fritzing sketch Square (saved by Fritzing 0.9.3b)
breadboards: 2

parts:
  Arduino2 = Arduino Uno (Rev3)
  C1 = Electrolytic Capacitor [capacitance=1µF package="100 mil [THT, electrolytic]"]
  R1 = Resistor [tolerance=±5% resistance=220 package=THT]

nets:
  N1: Arduino2.A3, C1.+, R1.Pin_1
  N2: Arduino2.GND, C1.-
  N3: Arduino2.D4, R1.Pin_0

notes:
  Output goes through resistor and capcitator. Yellow line messures voltage between the two

// code stored in the sketch: MeasureSquareWave.ino
// Visual Micro is in vMicro>General>Tutorial Mode
// 
/*
    Name:       MeasureSquareWave.ino
    Created:	2018-11-11 13:34:26
    Author:     CALCITE\leifl
*/

// Define User Types below here or use a .h file
//


// Define Function Prototypes that use User Types below here or use a .h file
//


// Define Functions below here or use other .ino or cpp files
//

// The setup() function runs once each time the micro-controller starts
void setup()
{


}

// Add the main program code into the continuous loop() function
void loop()
{


}
